# Fritzing sketch Board-Sensors-Tx (saved by Fritzing 0.9.2b)
circuit board: 5cm x 5cm
breadboards: 1

parts:
  RFM12b2 = RFM12b HopeRF Transceiver
  - = female pin header, 1 pin [form="♀ (female)"]
  + = female pin header, 1 pin [form="♀ (female)"]
  T = female pin header, 1 pin [form="♀ (female)"]
  T-8-4_7k = Resistor [tolerance=±1% resistance=4.7k package="0805 [SMD]"]
  L0-200k = Resistor [tolerance=±1% resistance=220k package="0805 [SMD]"]
  I3/4-10M = Resistor [tolerance=±1% resistance=4.7k package="0805 [SMD]"]
  +DHT22 = female pin header, 4 pins [form="♀ (female)"]
  +DS18 = female pin header, 3 pins [form="♀ (female)"]
  FTDI = female pin header, 6 pins [form="♀ (female)"]  # not connected
  9_8_7_6_5_4_3_2_G = female pin header, 9 pins [form="♀ (female)"]
  I2C = female pin header, 2 pins [form="♀ (female)"]
  CL_DA_-_+ = female pin header, 4 pins [form="♀ (female)"]
  10_11_12_13_A0_A1 = female pin header, 6 pins [form="♀ (female)"]
  +_Rst_-_(+) = female pin header, 4 pins [form="♀ (female)"]
  +_-_CL_DA = female pin header, 4 pins [form="♀ (female)"]
  part = female pin header, 2 pins [form="♀ (female)"]
  part_2 = Resistor [tolerance=±1% resistance=4.7k package="0805 [SMD]"]
  I3/4+ = female pin header, 2 pins [form="♀ (female)"]
  L0+ = female pin header, 2 pins [form="♀ (female)"]
  S1-10k = Resistor [tolerance=±1% resistance=4.7k package="0805 [SMD]"]
  part_3 = female pin header, 1 pin [form="♀ (female)"]
  part_4 = female pin header, 1 pin [form="♀ (female)"]
  part_5 = female pin header, 1 pin [form="♀ (female)"]
  part_6 = female pin header, 1 pin [form="♀ (female)"]
  D1 = Diode [package=sma-diode]
  JP14 = Header 1 [package=1x01_offset]
  JP13 = Header 1 [package=1x01_offset]
  JP12 = Header 1 [package=1x01_offset]
  JP15 = Header 1 [package=1x01_offset]
  JP16 = Header 1 [package=1x01_offset]
  part_7 = female pin header, 3 pins [form="♀ (female)"]  # not connected
  S1+ = female pin header, 3 pins [form="♀ (female)"]
  DA_CL_-_+ = female pin header, 4 pins [form="♀ (female)"]
  I/O = female pin header, 3 pins [form="♀ (female)"]
  4_7k = Resistor [tolerance=±1% resistance=4.7k package="0805 [SMD]"]
  4_7k_2 = Resistor [tolerance=±1% resistance=4.7k package="0805 [SMD]"]

nets:
  N1: RFM12b2.1_SDO, 10_11_12_13_A0_A1.pin3
  N2: RFM12b2.2_nIRQ, 9_8_7_6_5_4_3_2_G.pin2
  N3: RFM12b2.7_GND, RFM12b2.10_GND, -.pin1, +DHT22.pin1, +DHT22.pin2, +DS18.pin1, CL_DA_-_+.pin3, +_Rst_-_(+).pin3, +_-_CL_DA.pin2, part_5.pin1, part_6.pin1, JP14.1, JP15.1, DA_CL_-_+.pin3
  N4: RFM12b2.8_ANT, T.pin1
  N5: RFM12b2.9_VDD, +.pin1, T-8-4_7k.Pin_0, +DHT22.pin4, +DS18.pin3, CL_DA_-_+.pin4, +_Rst_-_(+).pin1, +_-_CL_DA.pin1, part.pin1, I3/4+.pin1, L0+.pin2, S1-10k.Pin_0, part_3.pin1, JP13.1, S1+.pin3, DA_CL_-_+.pin4, 4_7k.Pin_0, 4_7k_2.Pin_0
  N6: RFM12b2.12_SDI, 10_11_12_13_A0_A1.pin2
  N7: RFM12b2.13_SCK, 10_11_12_13_A0_A1.pin4
  N8: RFM12b2.14_nSEL, 10_11_12_13_A0_A1.pin1
  N9: T-8-4_7k.Pin_1, +DS18.pin2, 9_8_7_6_5_4_3_2_G.pin8
  N10: L0-200k.Pin_0, 10_11_12_13_A0_A1.pin5, L0+.pin1
  N11: L0-200k.Pin_1, I3/4-10M.Pin_1, 9_8_7_6_5_4_3_2_G.pin1, part_2.Pin_1, S1+.pin1
  N12: I3/4-10M.Pin_0, 9_8_7_6_5_4_3_2_G.pin4, part.pin2
  N13: +DHT22.pin3, 9_8_7_6_5_4_3_2_G.pin9
  N14: 9_8_7_6_5_4_3_2_G.pin3, part_2.Pin_0, I3/4+.pin2
  N15: 9_8_7_6_5_4_3_2_G.pin5, I/O.pin3
  N16: 9_8_7_6_5_4_3_2_G.pin6, I/O.pin2
  N17: 9_8_7_6_5_4_3_2_G.pin7, I/O.pin1
  N18: I2C.pin1, CL_DA_-_+.pin2, +_-_CL_DA.pin4, DA_CL_-_+.pin1, 4_7k.Pin_1
  N19: I2C.pin2, CL_DA_-_+.pin1, +_-_CL_DA.pin3, DA_CL_-_+.pin2, 4_7k_2.Pin_1
  N20: 10_11_12_13_A0_A1.pin6, S1-10k.Pin_1, S1+.pin2
  N21: +_Rst_-_(+).pin4, JP12.1
  N22: part_4.pin1, D1.C
  N23: D1.A, JP16.1

notes:
  +
  Kalemena
  Sensor - v2

custom parts:
  RFM12b HopeRF Transceiver: RF Transceiver by Hope RF. Well supported Arduino libraries are available. Part is available in several frequencies (433MHz, 915MHz)...
